// Logisim project Rai_Assignment_1.circ as structural Verilog: 1 circuit, main circuit main
module main (
);

  wire clock_1_out;
  wire [7:0] adder_1_out, register_1_q;

  Register register_1 (.D(adder_1_out), .en(1'b1), .Q(register_1_q), .clk(clock_1_out), .clr(1'b0));
  Clock clock_1 (.out(clock_1_out));
  Adder adder_1 (.a(register_1_q), .b(8'h1), .out(adder_1_out));  // open: cin, cout
  Hex_Digit_Display hex_digit_display_1 (.value(register_1_q[7:4]));  // open: dp
  Hex_Digit_Display hex_digit_display_2 (.value(register_1_q[3:0]));  // open: dp
endmodule
