// Logisim project Rai_Assignment_12.circ as structural Verilog: 1 circuit, main circuit main
module main (
);

  wire and_1_out, clock_1_out, comparator_1_eq, comparator_1_gt, comparator_1_lt, decoder_1_out1,
       decoder_1_out2, decoder_1_out3, decoder_1_out4, decoder_1_out5, decoder_1_out6, decoder_1_out7,
       multiplexer_2_out, not_1_out, not_2_out, or_1_out, or_2_out, or_3_out, or_4_out, stallablememory_1_p7,
       xnor_1_out;
  wire [1:0] ram_1_data_2;
  wire [2:0] bit_extender_3_out;
  wire [6:0] multiplexer_3_out, register_2_q;
  wire [7:0] bit_extender_2_out, divider_1_out, divider_1_rem, multiplexer_4_out, multiplexer_5_out,
       multiplexer_6_out, ram_2_data, stallablememory_1_p1, stallablememory_1_p6;
  wire [7:7] register_2_q_2;
  wire [14:0] ram_1_data;
  wire [15:0] adder_1_out, bit_extender_1_out, multiplexer_1_out, register_1_q;

  Clock clock_1 (.out(clock_1_out));
  or or_1 (or_1_out, decoder_1_out5, decoder_1_out7);
  not not_1 (not_1_out, xnor_1_out);
  LED led_1 (.in(not_1_out));
  Register #(.width(16)) register_1 (.D(adder_1_out), .en(xnor_1_out), .Q(register_1_q), .clk(clock_1_out), .clr(1'b0));
  Multiplexer #(.width(16), .enable("false")) multiplexer_1 (
    .in0(16'h1), .in1(bit_extender_1_out), .out(multiplexer_1_out), .sel(and_1_out));
  and and_1 (and_1_out, decoder_1_out3, multiplexer_2_out);
  xnor xnor_1 (xnor_1_out, or_1_out, stallablememory_1_p7);
  Adder #(.width(16)) adder_1 (.a(register_1_q), .b(multiplexer_1_out), .out(adder_1_out));  // open: cin, cout
  not not_2 (not_2_out, comparator_1_eq);
  Multiplexer #(.enable("false")) multiplexer_2 (
    .in0(not_2_out), .in1(comparator_1_eq), .out(multiplexer_2_out), .sel(ram_1_data[7]));
  RAM #(.addrWidth(16), .dataWidth(16), .bus("separate")) ram_1 (
    .addr(register_1_q), .data({ram_1_data_2[0], ram_1_data}), .str(1'b0), .clk(clock_1_out));  // open: din, sel, ld, clr
  Hex_Digit_Display hex_digit_display_1 (.value(register_1_q[15:12]));  // open: dp
  assign bit_extender_1_out = {{8{ram_1_data_2[0]}}, {ram_1_data_2[0], ram_1_data[14:8]}};  // Bit_Extender bit_extender_1
  Hex_Digit_Display hex_digit_display_2 (.value(register_1_q[7:4]));  // open: dp
  Hex_Digit_Display hex_digit_display_3 (.value(register_1_q[11:8]));  // open: dp
  Decoder #(.select(3), .enable("false")) decoder_1 (
    .out0(ram_1_data_2[1]), .out1(decoder_1_out1), .out2(decoder_1_out2), .out3(decoder_1_out3),
    .out4(decoder_1_out4), .out5(decoder_1_out5), .out6(decoder_1_out6), .out7(decoder_1_out7),
    .sel(ram_1_data[2:0]));
  Multiplexer #(.width(7), .enable("false")) multiplexer_3 (
    .in0(ram_1_data[14:8]), .in1(register_2_q), .out(multiplexer_3_out), .sel(ram_1_data_2[0]));
  Hex_Digit_Display hex_digit_display_4 (.value(register_1_q[3:0]));  // open: dp
  or or_2 (or_2_out, ram_1_data_2[1], decoder_1_out1, decoder_1_out2, decoder_1_out5);
  TTY tty_1 (.data(multiplexer_3_out), .clk(clock_1_out), .we(decoder_1_out6), .clr(1'b0));
  Register register_2 (
    .D(multiplexer_6_out), .en(or_2_out), .Q({register_2_q_2[7], register_2_q}), .clk(clock_1_out));  // open: clr
  Comparator comparator_1 (
    .a(ram_2_data), .b({register_2_q_2[7], register_2_q}), .gt(comparator_1_gt), .eq(comparator_1_eq),
    .lt(comparator_1_lt));
  or or_3 (or_3_out, decoder_1_out1, decoder_1_out7, decoder_1_out5);
  Hex_Digit_Display hex_digit_display_5 (.value(register_2_q[3:0]));  // open: dp
  Hex_Digit_Display hex_digit_display_6 (.value({register_2_q_2[7], register_2_q[6:4]}));  // open: dp
  // StallableMemory stallablememory_1: pin names not known; wires that end beside it: stallablememory_1_p1, {register_2_q_2[7], register_2_q}, decoder_1_out7, decoder_1_out5, clock_1_out, stallablememory_1_p6, stallablememory_1_p7
  RAM #(.addrWidth(3), .bus("separate")) ram_2 (
    .addr(ram_1_data[5:3]), .din({register_2_q_2[7], register_2_q}), .data(ram_2_data), .str(decoder_1_out4),
    .clk(clock_1_out), .ld(or_4_out));  // open: sel, clr
  Adder adder_2 (.a(ram_2_data), .b(multiplexer_4_out), .out(stallablememory_1_p1));  // open: cin, cout
  Multiplexer #(.width(8), .enable("false")) multiplexer_4 (
    .in0({register_2_q_2[7], register_2_q}), .in1({ram_1_data_2[0], ram_1_data[14:8]}),
    .out(multiplexer_4_out), .sel(or_3_out));
  Multiplexer #(.width(8), .enable("false")) multiplexer_5 (
    .in0(stallablememory_1_p1), .in1(stallablememory_1_p6), .out(multiplexer_5_out), .sel(decoder_1_out5));
  Divider divider_1 (
    .a({register_2_q_2[7], register_2_q}), .b(bit_extender_2_out), .out(divider_1_out), .upper({8{1'b0}}),
    .rem(divider_1_rem));
  or or_4 (or_4_out, or_2_out, decoder_1_out3, decoder_1_out7);
  assign bit_extender_2_out = {{1{ram_1_data[14]}}, ram_1_data[14:8]};  // Bit_Extender bit_extender_2
  Multiplexer #(.select(3), .width(8), .enable("false")) multiplexer_6 (
    .in0(multiplexer_5_out), .in1(multiplexer_5_out), .in2(divider_1_out), .in3(divider_1_rem),
    .out(multiplexer_6_out), .sel(bit_extender_3_out));  // open: in4, in5, in6, in7
  assign bit_extender_3_out = {{1{1'b0}}, ram_1_data_2};  // Bit_Extender bit_extender_3

  // Notes on the sheet:
  //   Reg and Accum: 02
  //   Jump: 03
  //   Reg and Immediate: 01
  //   Store Register File: 04
  //   Load Data Memory Into Accum: 05
  //   Store in Data Memory: 07
  //   00 Is Division and Remainder, Remainder Requires MSB of Immediate as 1
  //   Bit 7 In Instruction Controls Equal or Not Equal Jump, Equal Requires 1
  //   TTY Write: 06
  //   Stall LED In Top Left
  //   Register File
  //   Data Memory
endmodule
