// Logisim project Rai_Assignment_4.circ as structural Verilog: 1 circuit, main circuit main
module main (
);

  wire clock_1_out;
  wire [3:0] multiplexer_2_out;
  wire [7:0] ram_1_data;
  wire [15:0] adder_1_out, multiplexer_1_out, register_1_q;

  Clock clock_1 (.out(clock_1_out));
  Register #(.width(16)) register_1 (.D(multiplexer_1_out), .en(1'b1), .Q(register_1_q), .clk(clock_1_out), .clr(1'b0));
  Multiplexer #(.width(16), .enable("false")) multiplexer_1 (
    .in0(adder_1_out), .in1(16'h2), .out(multiplexer_1_out), .sel(ram_1_data[3]));
  Adder #(.width(16)) adder_1 (.a(register_1_q), .b(16'h1), .out(adder_1_out));  // open: cin, cout
  RAM #(.addrWidth(16), .bus("separate")) ram_1 (
    .addr(register_1_q), .data(ram_1_data), .str(1'b0), .clk(clock_1_out));  // open: din, sel, ld, clr
  Hex_Digit_Display hex_digit_display_1 (.value(register_1_q[15:12]));  // open: dp
  Hex_Digit_Display hex_digit_display_2 (.value(register_1_q[7:4]));  // open: dp
  Hex_Digit_Display hex_digit_display_3 (.value(register_1_q[11:8]));  // open: dp
  Hex_Digit_Display hex_digit_display_4 (.value(register_1_q[3:0]));  // open: dp
  Multiplexer #(.width(4), .enable("false")) multiplexer_2 (
    .in0(4'b1010), .in1(4'b0111), .out(multiplexer_2_out), .sel(ram_1_data[2]));
  Hex_Digit_Display hex_digit_display_5 (.value(multiplexer_2_out));  // open: dp
endmodule
