// Logisim project Rai_Assignment_5.circ as structural Verilog: 1 circuit, main circuit main
module main (
);

  wire clock_1_out;
  wire [6:0] bit_extender_2_out;
  wire [15:0] adder_1_out, bit_extender_1_out, multiplexer_1_out, ram_1_data, register_1_q;

  Clock clock_1 (.out(clock_1_out));
  Register #(.width(16)) register_1 (.D(adder_1_out), .en(1'b1), .Q(register_1_q), .clk(clock_1_out), .clr(1'b0));
  Multiplexer #(.width(16), .enable("false")) multiplexer_1 (
    .in0(16'h1), .in1(bit_extender_1_out), .out(multiplexer_1_out), .sel(ram_1_data[2]));
  Adder #(.width(16)) adder_1 (.a(register_1_q), .b(multiplexer_1_out), .out(adder_1_out));  // open: cin, cout
  RAM #(.addrWidth(16), .dataWidth(16), .bus("separate")) ram_1 (
    .addr(register_1_q), .data(ram_1_data), .str(1'b0), .clk(clock_1_out));  // open: din, sel, ld, clr
  Hex_Digit_Display hex_digit_display_1 (.value(register_1_q[15:12]));  // open: dp
  assign bit_extender_1_out = {{8{ram_1_data[15]}}, ram_1_data[15:8]};  // Bit_Extender bit_extender_1
  Hex_Digit_Display hex_digit_display_2 (.value(register_1_q[11:8]));  // open: dp
  Hex_Digit_Display hex_digit_display_3 (.value(register_1_q[7:4]));  // open: dp
  Bit_Extender #(.out_width(7)) bit_extender_2 (.in(ram_1_data[15:8]), .out(bit_extender_2_out));
  Hex_Digit_Display hex_digit_display_4 (.value(register_1_q[3:0]));  // open: dp
  TTY tty_1 (.data(bit_extender_2_out), .clk(clock_1_out), .we(ram_1_data[0]), .clr(1'b0));
endmodule
