// Logisim project Rai_Assignment_7.circ as structural Verilog: 1 circuit, main circuit main
module main (
);

  wire clock_1_out, decoder_1_out1, decoder_1_out2, decoder_1_out3, decoder_1_out4, decoder_1_out6, or_1_out;
  wire [6:0] bit_extender_2_out;
  wire [7:0] adder_2_out, multiplexer_2_out, ram_2_data, register_2_q;
  wire [15:0] adder_1_out, bit_extender_1_out, multiplexer_1_out, ram_1_data, register_1_q;

  Clock clock_1 (.out(clock_1_out));
  Register #(.width(16)) register_1 (.D(adder_1_out), .en(1'b1), .Q(register_1_q), .clk(clock_1_out), .clr(1'b0));
  Multiplexer #(.width(16), .enable("false")) multiplexer_1 (
    .in0(16'h1), .in1(bit_extender_1_out), .out(multiplexer_1_out), .sel(decoder_1_out3));
  Adder #(.width(16)) adder_1 (.a(register_1_q), .b(multiplexer_1_out), .out(adder_1_out));  // open: cin, cout
  RAM #(.addrWidth(16), .dataWidth(16), .bus("separate")) ram_1 (
    .addr(register_1_q), .data(ram_1_data), .str(1'b0), .clk(clock_1_out));  // open: din, sel, ld, clr
  Hex_Digit_Display hex_digit_display_1 (.value(register_1_q[15:12]));  // open: dp
  assign bit_extender_1_out = {{8{ram_1_data[15]}}, ram_1_data[15:8]};  // Bit_Extender bit_extender_1
  Hex_Digit_Display hex_digit_display_2 (.value(register_1_q[7:4]));  // open: dp
  Hex_Digit_Display hex_digit_display_3 (.value(register_1_q[11:8]));  // open: dp
  Decoder #(.select(3), .enable("false")) decoder_1 (
    .out1(decoder_1_out1), .out2(decoder_1_out2), .out3(decoder_1_out3), .out4(decoder_1_out4),
    .out6(decoder_1_out6), .sel(ram_1_data[2:0]));  // open: out0, out5, out7
  Bit_Extender #(.out_width(7)) bit_extender_2 (.in(ram_1_data[15:8]), .out(bit_extender_2_out));
  Hex_Digit_Display hex_digit_display_4 (.value(register_1_q[3:0]));  // open: dp
  or or_1 (or_1_out, decoder_1_out1, decoder_1_out2);
  TTY tty_1 (.data(bit_extender_2_out), .clk(clock_1_out), .we(decoder_1_out6), .clr(1'b0));
  Register register_2 (.D(adder_2_out), .en(or_1_out), .Q(register_2_q), .clk(clock_1_out));  // open: clr
  Hex_Digit_Display hex_digit_display_5 (.value(register_2_q[7:4]));  // open: dp
  Hex_Digit_Display hex_digit_display_6 (.value(register_2_q[3:0]));  // open: dp
  RAM #(.addrWidth(3), .bus("separate")) ram_2 (
    .addr(ram_1_data[5:3]), .din(register_2_q), .data(ram_2_data), .str(decoder_1_out4), .clk(clock_1_out),
    .ld(or_1_out));  // open: sel, clr
  Adder adder_2 (.a(ram_2_data), .b(multiplexer_2_out), .out(adder_2_out));  // open: cin, cout
  Multiplexer #(.width(8), .enable("false")) multiplexer_2 (
    .in0(register_2_q), .in1(ram_1_data[15:8]), .out(multiplexer_2_out), .sel(decoder_1_out1));

  // Notes on the sheet:
  //   Register: Bits 3-5
  //   Jump: 03
  //   Write: 06
  //   Store: 04
  //   Register File
  //   Reg and Immediate: 01
  //   Reg and Accum: 02
endmodule
